# Fritzing sketch Visual eletrical design light switch case (saved by Fritzing 0.9.3b)
breadboards: 1

parts:
  A1 = DFR Sen0539-EN
  Part1 = Arduino Nano (Rev3.0)
  J1 = Basic Servo
  J2 = Basic Servo
  U1 = SWITCH-SPST-2 [package=switch-spst-vertical]
  VCC1 = Battery block 9V
  IC2 = Voltage Regulator [package=78xxl]
  C2 = Electrolytic Capacitor [capacitance=10µF voltage=50V package="100 mil [THT, electrolytic]"]
  C3 = Electrolytic Capacitor [capacitance=10µF voltage=50V package="100 mil [THT, electrolytic]"]
  C5 = Ceramic Capacitor [capacitance=0.1µF package="100 mil [THT, multilayer]"]
  Q3 = Basic FET P-Channel [package="DPak [SMD]"]
  C6 = Ceramic Capacitor [capacitance=0.1µF package="1206 [SMD, multilayer]"]
  C7 = Ceramic Capacitor [capacitance=1µF package="0603 [SMD, multilayer]"]
  C8 = Ceramic Capacitor [capacitance=1µF package="0603 [SMD, multilayer]"]
  R1 = Resistor [tolerance=±5% resistance=10k package=THT]
  R2 = Resistor [tolerance=±5% resistance=10k package=THT]
  D3 = Rectifier Diode [part_number=1N4001 package="Melf DO-213 AB [SMD]"]
  LED1 = LED - 3mm [color="Red (633nm)" package="3 mm [THT]"]
  R3 = Resistor [tolerance=±5% resistance=220 package=THT]

nets:
  N1: A1.Pin_1, Part1.D4
  N2: A1.Pin_2, Part1.D5
  GND: A1.Pin_3, Part1.GND, J1.gnd, J2.gnd, VCC1.-, IC2.GND, C2.-, C3.+, C5.0, C6.1, C7.0, C8.0, LED1.cathode
  N3: A1.Pin_4, Part1.5V
  N4: Part1.D10, R1.Pin_0
  N5: Part1.VIN, U1.O, Q3.source, R2.Pin_1
  VCC: J1.vcc, J2.vcc, IC2.OUT, C2.+, C5.1, C7.1, C8.1, D3.anode, R3.Pin_1
  N6: U1.P, VCC1.+
  N7: IC2.IN, C3.-, Q3.drain, C6.0, D3.cathode
  N8: Q3.Gate, R1.Pin_1, R2.Pin_0
  N9: LED1.anode, R3.Pin_0

custom parts:
  DFR Sen0539-EN: Offline Language Learning Voice Recognition Sensor.
